# Fritzing sketch chirp (saved by Fritzing 0.9.3b)
breadboards: 1

parts:
  Raspberry_Pi_1 = Raspberry Pi 3 [part_number=RPI-3-V1.2]
  Part2 = LSM303C (6 DOF)

nets:
  N1: Raspberry_Pi_1.3v3, Part2.VDD_IO
  N2: Raspberry_Pi_1.GPIO2, Part2.SDA/SDI/SDO
  N3: Raspberry_Pi_1.GPIO3, Part2.SCL/SCLK
  GND: Raspberry_Pi_1.GND, Part2.GND
